// Logisim project 0701.circ as structural Verilog: 1 circuit, main circuit main
module main (
  input  in_1,
  input  in_2,
  input  in_3,
  input  a,
  input  b,
  input  sel,
  output out_7,
  output y
);

  wire and_1_out, and_2_out, and_3_out, and_4_out, and_5_out, nand_1_out, not_1_out, not_2_out;

  nand nand_1 (nand_1_out, a, b);
  and and_1 (and_1_out, a, b);
  and and_2 (and_2_out, in_1, not_1_out);
  not not_1 (not_1_out, in_3);
  and and_3 (and_3_out, in_2, in_3);
  not not_2 (not_2_out, sel);
  or or_1 (out_7, and_2_out, and_3_out);
  and and_4 (and_4_out, nand_1_out, not_2_out);
  and and_5 (and_5_out, and_1_out, sel);
  or or_2 (y, and_4_out, and_5_out);

  // Notes on the sheet:
  //   Multiplexador
  //   y0
  //   y1
  //   Circuito final NAND e AND com seleção via multiplexador
  //   mux0
  //   mux1
endmodule
