// Logisim project 0702.circ as structural Verilog: 1 circuit, main circuit main
module main (
  input  a,
  input  b,
  input  selec,
  output s
);

  wire and_1_out, and_2_out, nor_1_out, not_1_out, or_1_out;

  or or_1 (or_1_out, a, b);
  nor nor_1 (nor_1_out, a, b);
  and and_1 (and_1_out, or_1_out, not_1_out);
  not not_1 (not_1_out, selec);
  and and_2 (and_2_out, nor_1_out, selec);
  or or_2 (s, and_1_out, and_2_out);

  // Notes on the sheet:
  //   nor
  //   or
  //   y0
  //   y1
  //   MUX
  //   mux0
  //   mux1
endmodule
