// Logisim project 0703.circ as structural Verilog: 1 circuit, main circuit main
module main (
  input  a,
  input  b,
  input  ctrl1,
  input  ctrl2,
  output out_5
);

  wire and_1_out, and_2_out, and_3_out, and_4_out, and_5_out, and_6_out, and_7_out, nand_1_out, nor_1_out,
       not_1_out, not_2_out, not_3_out, or_1_out, or_2_out, or_3_out;

  and and_1 (and_1_out, a, b);
  nand nand_1 (nand_1_out, a, b);
  or or_1 (or_1_out, a, b);
  nor nor_1 (nor_1_out, a, b);
  and and_2 (and_2_out, and_1_out, not_1_out);
  not not_1 (not_1_out, ctrl1);
  and and_3 (and_3_out, nand_1_out, ctrl1);
  and and_4 (and_4_out, or_1_out, not_2_out);
  not not_2 (not_2_out, ctrl1);
  and and_5 (and_5_out, nor_1_out, ctrl1);
  or or_2 (or_2_out, and_2_out, and_3_out);
  not not_3 (not_3_out, ctrl2);
  or or_3 (or_3_out, and_4_out, and_5_out);
  and and_6 (and_6_out, or_2_out, not_3_out);
  and and_7 (and_7_out, ctrl2, or_3_out);
  or or_4 (out_5, and_6_out, and_7_out);

  // Notes on the sheet:
  //   mux0
  //   mux1
  //   mux3
endmodule
