// Logisim project 0704.circ as structural Verilog: 1 circuit, main circuit main
module main (
  input  a,
  input  b,
  input  in_3,
  input  in_4,
  output out_5
);

  wire and_1_out, and_2_out, and_3_out, and_4_out, nor_1_out, not_1_out, not_2_out, not_3_out, not_4_out,
       or_1_out, xnor_1_out, xor_1_out;

  xor xor_1 (xor_1_out, a, b);
  xnor xnor_1 (xnor_1_out, a, b);
  or or_1 (or_1_out, a, b);
  nor nor_1 (nor_1_out, a, b);
  and and_1 (and_1_out, xor_1_out, not_1_out, not_2_out);
  not not_1 (not_1_out, in_3);
  not not_2 (not_2_out, in_4);
  and and_2 (and_2_out, xnor_1_out, not_3_out, in_4);
  not not_3 (not_3_out, in_3);
  and and_3 (and_3_out, or_1_out, in_3, not_4_out);
  not not_4 (not_4_out, in_4);
  and and_4 (and_4_out, nor_1_out, in_3, in_4);
  or or_2 (out_5, and_1_out, and_2_out, and_3_out, and_4_out);

  // Notes on the sheet:
  //   Multiplexador
endmodule
