// Logisim project 0801.circ as structural Verilog: 1 circuit, main circuit main
module main (
  input  a5,
  input  a4,
  input  a3,
  input  b5,
  input  b4,
  input  b3,
  input  c5,
  input  a2,
  input  a1,
  input  a1_2,
  input  b2,
  input  b,
  input  b_2,
  output s6,
  output s5,
  output s4,
  output s3,
  output s2,
  output s0,
  output s1
);

  wire and_1_out, and_2_out, and_3_out, and_4_out, and_5_out, and_6_out, and_7_out, and_8_out, and_9_out,
       and_10_out, and_11_out, and_12_out, or_2_out, or_3_out, or_4_out, or_5_out, or_6_out, xor_2_out,
       xor_3_out, xor_6_out, xor_7_out, xor_10_out, xor_11_out;

  or or_1 (s0, and_1_out, and_2_out);
  xor xor_1 (s1, xor_2_out, or_3_out);
  and and_1 (and_1_out, xor_2_out, or_3_out);
  and and_2 (and_2_out, b_2, a1_2);
  xor xor_2 (xor_2_out, a1_2, b_2);
  xor xor_3 (xor_3_out, a5, b5);
  and and_3 (and_3_out, b5, a5);
  xor xor_4 (s6, xor_3_out, c5);
  and and_4 (and_4_out, c5, xor_3_out);
  or or_2 (or_2_out, and_4_out, and_3_out);
  or or_3 (or_3_out, and_5_out, and_6_out);
  xor xor_5 (s2, xor_6_out, or_5_out);
  and and_5 (and_5_out, xor_6_out, or_5_out);
  xor xor_6 (xor_6_out, a1, b);
  and and_6 (and_6_out, b, a1);
  xor xor_7 (xor_7_out, a4, b4);
  and and_7 (and_7_out, b4, a4);
  xor xor_8 (s5, xor_7_out, or_2_out);
  and and_8 (and_8_out, or_2_out, xor_7_out);
  or or_4 (or_4_out, and_8_out, and_7_out);
  or or_5 (or_5_out, and_9_out, and_10_out);
  xor xor_9 (s3, xor_11_out, or_6_out);
  and and_9 (and_9_out, xor_11_out, or_6_out);
  and and_10 (and_10_out, b2, a2);
  xor xor_10 (xor_10_out, a3, b3);
  and and_11 (and_11_out, b3, a3);
  xor xor_11 (xor_11_out, a2, b2);
  and and_12 (and_12_out, or_4_out, xor_10_out);
  xor xor_12 (s4, xor_10_out, or_4_out);
  or or_6 (or_6_out, and_12_out, and_11_out);

  // Notes on the sheet:
  //   c1
  //   c4
  //   6-bit-Full-adder
  //   Resposta => numero formado pelos bits [s0,s1,s2,s3s4,s5]
  //   c1
  //   c3
  //   c2
endmodule
