// Logisim project 0802.circ as structural Verilog: 1 circuit, main circuit main
module main (
  input  x,
  input  x_2,
  input  emprestou,
  input  y,
  input  y_2,
  input  x_3,
  input  y_3,
  input  x_4,
  input  x_5,
  input  y_4,
  input  y_5,
  output s0,
  output s1,
  output s2,
  output s3,
  output s4,
  output out_17
);

  wire and_1_out, and_2_out, and_3_out, and_4_out, and_5_out, and_6_out, and_7_out, and_8_out, and_9_out,
       and_10_out, not_1_out, not_2_out, not_3_out, not_4_out, not_5_out, not_6_out, not_7_out, not_8_out,
       not_9_out, not_10_out, or_1_out, or_3_out, or_4_out, or_5_out, xor_1_out, xor_4_out, xor_5_out,
       xor_8_out, xor_9_out;

  xor xor_1 (xor_1_out, x, y);
  not not_1 (not_1_out, x);
  xor xor_2 (s0, xor_1_out, emprestou);
  not not_2 (not_2_out, xor_1_out);
  and and_1 (and_1_out, not_2_out, emprestou);
  and and_2 (and_2_out, y, not_1_out);
  or or_1 (or_1_out, and_1_out, and_2_out);
  or or_2 (out_17, and_3_out, and_4_out);
  xor xor_3 (s4, xor_4_out, or_4_out);
  not not_3 (not_3_out, xor_4_out);
  and and_3 (and_3_out, not_3_out, or_4_out);
  xor xor_4 (xor_4_out, x_5, y_5);
  and and_4 (and_4_out, y_5, not_4_out);
  not not_4 (not_4_out, x_5);
  xor xor_5 (xor_5_out, x_2, y_2);
  xor xor_6 (s1, xor_5_out, or_1_out);
  not not_5 (not_5_out, xor_5_out);
  and and_5 (and_5_out, not_5_out, or_1_out);
  and and_6 (and_6_out, y_2, not_6_out);
  not not_6 (not_6_out, x_2);
  or or_3 (or_3_out, and_5_out, and_6_out);
  or or_4 (or_4_out, and_7_out, and_8_out);
  xor xor_7 (s3, xor_8_out, or_5_out);
  and and_7 (and_7_out, not_7_out, or_5_out);
  xor xor_8 (xor_8_out, x_4, y_4);
  not not_7 (not_7_out, xor_8_out);
  and and_8 (and_8_out, y_4, not_8_out);
  not not_8 (not_8_out, x_4);
  xor xor_9 (xor_9_out, x_3, y_3);
  not not_9 (not_9_out, xor_9_out);
  and and_9 (and_9_out, y_3, not_10_out);
  not not_10 (not_10_out, x_3);
  xor xor_10 (s2, xor_9_out, or_3_out);
  and and_10 (and_10_out, not_9_out, or_3_out);
  or or_5 (or_5_out, and_10_out, and_9_out);

  // Notes on the sheet:
  //   s5 (sempre zero)
  //   pegou emprestado
  //   Pegou emprestado
  //   emprestou
  //   Teste para circuito subtrator completo 6bits
  //   Teste realizado subtraindo: 10110  - 10011
  //   Resultado esperado: 00011
  //   Resultado obtido: (s5) s4s3s2s1s0
  //   emprestou
  //   Pegou emprestado
  //   pegou emprestado
  //   emprestou
  //   emprestou
  //   pegou emprestado
endmodule
