// Logisim project 0803.circ as structural Verilog: 1 circuit, main circuit main
module main (
  input  in_1,
  input  in_2,
  input  in_3,
  input  in_4,
  input  in_5,
  input  in_6,
  input  in_7,
  input  in_8,
  input  in_9,
  input  in_10,
  input  in_11,
  input  in_12,
  output s3,
  output s1,
  output out_15,
  output out_16,
  output out_17,
  output out_18
);

  xnor xnor_1 (s1, in_2, in_5);
  xnor xnor_2 (out_18, in_9, in_12);
  xnor xnor_3 (out_15, in_3, in_6);
  xnor xnor_4 (out_17, in_8, in_11);
  xnor xnor_5 (s3, in_1, in_4);
  xnor xnor_6 (out_16, in_7, in_10);

  // Notes on the sheet:
  //   s4
  //   Unidade Lógica para checagem de Igualdade 
  //   Números iguais se f(s1,s2,s3,s4,s5,s6) = 1
  //   Numeros diferentes se f(s1|s2|s3|s4|s5|s6) = 0
  //   Teste feito com o numeros 101001 & 101001
  //   s2
  //   s5
  //   s6
endmodule
