// Logisim project 0804.circ as structural Verilog: 1 circuit, main circuit main
module main (
  input  in_1,
  input  in_2,
  input  in_3,
  input  in_4,
  input  in_5,
  input  in_6,
  input  in_7,
  input  in_8,
  input  in_9,
  input  in_10,
  input  in_11,
  input  in_12,
  output s0,
  output s1,
  output s2,
  output s3,
  output s4,
  output s5
);

  xor xor_1 (s5, in_9, in_12);
  xor xor_2 (s0, in_1, in_4);
  xor xor_3 (s1, in_2, in_5);
  xor xor_4 (s4, in_8, in_11);
  xor xor_5 (s2, in_3, in_6);
  xor xor_6 (s3, in_7, in_10);

  // Notes on the sheet:
  //   Teste com os numeros 100101 e 100111
  //   Comparador de desigualdade
  //   Se pelo menos uma das saidas (Sn) for igual a 1, os numeros são distintos
endmodule
