// Logisim project 0805.circ as structural Verilog: 2 circuits, main circuit main
module main (
  input  in_1,
  input  in_2,
  input  in_3,
  input  in_4,
  input  in_5,
  input  in_6,
  input  in_7,
  input  in_8,
  input  in_9,
  input  in_10,
  input  in_11,
  input  in_12,
  input  in_13,
  output out_14,
  output out_15,
  output out_16,
  output out_17,
  output out_18,
  output out_19,
  output out_20
);

  wire not_1_out, not_2_out, not_3_out, not_4_out, not_5_out, not_6_out;

  not not_1 (not_1_out, in_2);
  not not_2 (not_2_out, in_1);
  not not_3 (not_3_out, in_5);
  not not_4 (not_4_out, in_4);
  not not_5 (not_5_out, in_6);
  not not_6 (not_6_out, in_3);
  _6BIT_adder u_6bit_adder_1 (
    .a0(not_5_out), .a1(not_3_out), .a2(not_4_out), .b0(in_12), .b1(in_11), .b2(in_10), .carry(in_13),
    .s0(out_14), .s1(out_15), .s6(out_20), .s2(out_16), .s5(out_19), .s3(out_17), .s4(out_18),
    .a3(not_6_out), .a4(not_1_out), .a5(not_2_out), .b3(in_9), .b4(in_8), .b5(in_7));

  // Notes on the sheet:
  //   Número de 6 bits a sofrer o complemento de 2
  //   Resultado do complemento de 2
  //   Somando + 1 ao complemento de 1
endmodule

// sum_6bit
module _6BIT_adder (
  input  a0,
  input  a1,
  input  a2,
  input  b0,
  input  b1,
  input  b2,
  input  carry,
  input  a3,
  input  a4,
  input  a5,
  input  b3,
  input  b4,
  input  b5,
  output s6,
  output s5,
  output s4,
  output s3,
  output s2,
  output s0,
  output s1
);

  wire and_1_out, and_2_out, and_3_out, and_4_out, and_5_out, and_6_out, and_7_out, and_8_out, and_9_out,
       and_10_out, and_11_out, and_12_out, or_2_out, or_3_out, or_4_out, or_5_out, or_6_out, xor_2_out,
       xor_3_out, xor_6_out, xor_7_out, xor_10_out, xor_11_out;

  xor xor_1 (s1, xor_2_out, or_3_out);
  and and_1 (and_1_out, xor_2_out, or_3_out);
  or or_1 (s0, and_1_out, and_2_out);
  xor xor_2 (xor_2_out, a5, b5);
  and and_2 (and_2_out, b5, a5);
  xor xor_3 (xor_3_out, a0, b0);
  and and_3 (and_3_out, b0, a0);
  and and_4 (and_4_out, carry, xor_3_out);
  xor xor_4 (s6, xor_3_out, carry);
  or or_2 (or_2_out, and_4_out, and_3_out);
  xor xor_5 (s2, xor_7_out, or_5_out);
  or or_3 (or_3_out, and_5_out, and_6_out);
  and and_5 (and_5_out, xor_7_out, or_5_out);
  and and_6 (and_6_out, b4, a4);
  xor xor_6 (xor_6_out, a1, b1);
  and and_7 (and_7_out, b1, a1);
  xor xor_7 (xor_7_out, a4, b4);
  and and_8 (and_8_out, or_2_out, xor_6_out);
  xor xor_8 (s5, xor_6_out, or_2_out);
  or or_4 (or_4_out, and_8_out, and_7_out);
  or or_5 (or_5_out, and_9_out, and_11_out);
  xor xor_9 (s3, xor_11_out, or_6_out);
  and and_9 (and_9_out, xor_11_out, or_6_out);
  xor xor_10 (xor_10_out, a2, b2);
  and and_10 (and_10_out, b2, a2);
  xor xor_11 (xor_11_out, a3, b3);
  and and_11 (and_11_out, b3, a3);
  and and_12 (and_12_out, or_4_out, xor_10_out);
  xor xor_12 (s4, xor_10_out, or_4_out);
  or or_6 (or_6_out, and_12_out, and_10_out);
endmodule
