// Logisim project 1201.circ as structural Verilog: 1 circuit, main circuit main
module main (
  input  in_1,
  input  in_2,
  input  in_3,
  input  in_4,
  input  in_5,
  input  in_6,
  input  in_7,
  input  in_8,
  input  in_9,
  input  in_10,
  input  in_11,
  input  in_12,
  input  R_W
);

  wire and_1_out, and_2_out, and_3_out, and_4_out, clock_1_out, j_k_ff_1_q, j_k_ff_2_q, j_k_ff_3_q,
       j_k_ff_4_q, multiplexer_1_out, multiplexer_2_out, multiplexer_3_out, multiplexer_4_out,
       multiplexer_5_out, multiplexer_6_out, multiplexer_7_out, multiplexer_8_out, not_1_out, not_2_out,
       not_3_out, not_4_out, not_5_out, not_6_out, not_7_out, not_8_out, or_1_out;

  Clock clock_1 (.out(clock_1_out));
  Multiplexer #(.enable("false")) multiplexer_1 (.in0(in_5), .in1(in_9), .out(multiplexer_1_out), .sel(R_W));
  J_K_Flip_Flop j_k_ff_1 (
    .J(multiplexer_1_out), .clk(clock_1_out), .K(multiplexer_2_out), .Q(j_k_ff_1_q));  // open: Qn, preset, reset
  Multiplexer #(.enable("false")) multiplexer_2 (.in0(in_6), .in1(not_1_out), .out(multiplexer_2_out), .sel(R_W));
  not not_1 (not_1_out, in_9);
  Multiplexer #(.enable("false")) multiplexer_3 (.in0(in_7), .in1(in_10), .out(multiplexer_3_out), .sel(R_W));
  J_K_Flip_Flop j_k_ff_2 (
    .J(multiplexer_3_out), .clk(clock_1_out), .K(multiplexer_4_out), .Q(j_k_ff_2_q));  // open: Qn, preset, reset
  Multiplexer #(.enable("false")) multiplexer_4 (.in0(in_8), .in1(not_2_out), .out(multiplexer_4_out), .sel(R_W));
  not not_2 (not_2_out, in_10);
  Multiplexer #(.enable("false")) multiplexer_5 (.in0(in_1), .in1(in_11), .out(multiplexer_5_out), .sel(R_W));
  J_K_Flip_Flop j_k_ff_3 (
    .J(multiplexer_5_out), .clk(clock_1_out), .K(multiplexer_6_out), .Q(j_k_ff_3_q));  // open: Qn, preset, reset
  Multiplexer #(.enable("false")) multiplexer_6 (.in0(in_2), .in1(not_3_out), .out(multiplexer_6_out), .sel(R_W));
  not not_3 (not_3_out, in_11);
  Multiplexer #(.enable("false")) multiplexer_7 (.in0(in_3), .in1(in_12), .out(multiplexer_7_out), .sel(R_W));
  J_K_Flip_Flop j_k_ff_4 (
    .J(multiplexer_7_out), .clk(clock_1_out), .K(multiplexer_8_out), .Q(j_k_ff_4_q));  // open: Qn, preset, reset
  Multiplexer #(.enable("false")) multiplexer_8 (.in0(in_4), .in1(not_4_out), .out(multiplexer_8_out), .sel(R_W));
  not not_4 (not_4_out, in_12);
  or or_1 (or_1_out, R_W, clock_1_out);
  not not_5 (not_5_out, or_1_out);
  and and_1 (and_1_out, not_5_out, j_k_ff_4_q);
  not not_6 (not_6_out, or_1_out);
  not not_7 (not_7_out, or_1_out);
  and and_2 (and_2_out, not_7_out, j_k_ff_3_q);
  and and_3 (and_3_out, not_6_out, j_k_ff_2_q);
  // Probe on and_4_out
  not not_8 (not_8_out, or_1_out);
  and and_4 (and_4_out, not_8_out, j_k_ff_1_q);
  // Probe on and_2_out
  // Probe on and_3_out
  // Probe on and_1_out
endmodule
