// Logisim project 1202.circ as structural Verilog: 4 circuits, main circuit main
module main (
  input  in_1,
  input  in_2,
  input  in_3,
  input  in_4,
  input  in_5,
  input  in_6,
  input  in_7,
  input  in_8,
  input  in_9
);

  wire and_1_out, and_2_out, and_3_out, and_4_out, and_5_out, and_6_out, and_7_out, and_8_out, clock_1_out,
       not_1_out, not_2_out, not_3_out, not_4_out, not_5_out, not_6_out, not_7_out, not_8_out, or_1_out,
       ram_1x8_1_s0, ram_1x8_1_s1, ram_1x8_1_s2, ram_1x8_1_s3, ram_1x8_1_s4, ram_1x8_1_s5, ram_1x8_1_s6,
       ram_1x8_1_s7;

  Clock clock_1 (.out(clock_1_out));
  RAM_1X8 ram_1x8_1 (
    .clock(clock_1_out), .s7(ram_1x8_1_s7), .s6(ram_1x8_1_s6), .s5(ram_1x8_1_s5), .s4(ram_1x8_1_s4),
    .s3(ram_1x8_1_s3), .s2(ram_1x8_1_s2), .s1(ram_1x8_1_s1), .s0(ram_1x8_1_s0), .bit7(in_1), .bit6(in_2),
    .bit5(in_3), .bit4(in_4), .bit3(in_5), .bit2(in_6), .bit1(in_7), .bit0(in_8), .R_W(in_9));
  or or_1 (or_1_out, clock_1_out, in_9);
  not not_1 (not_1_out, or_1_out);
  not not_2 (not_2_out, or_1_out);
  and and_1 (and_1_out, not_2_out, ram_1x8_1_s0);
  and and_2 (and_2_out, not_1_out, ram_1x8_1_s1);
  not not_3 (not_3_out, or_1_out);
  not not_4 (not_4_out, or_1_out);
  not not_5 (not_5_out, or_1_out);
  and and_3 (and_3_out, not_3_out, ram_1x8_1_s2);
  and and_4 (and_4_out, not_4_out, ram_1x8_1_s4);
  and and_5 (and_5_out, not_5_out, ram_1x8_1_s3);
  // Probe on and_6_out
  // Probe on and_8_out
  // Probe on and_7_out
  not not_6 (not_6_out, or_1_out);
  not not_7 (not_7_out, or_1_out);
  not not_8 (not_8_out, or_1_out);
  and and_6 (and_6_out, not_8_out, ram_1x8_1_s6);
  and and_7 (and_7_out, not_6_out, ram_1x8_1_s5);
  // Probe on and_2_out
  // Probe on and_3_out
  // Probe on and_5_out
  // Probe on and_4_out
  and and_8 (and_8_out, not_7_out, ram_1x8_1_s7);
  // Probe on and_1_out
endmodule

module RAM_1x2 (
  input  clock,
  input  IGNORE,
  input  bit1,
  input  bit0,
  input  r_w,
  output s1,
  output s0
);

  wire multiplexer_1_out, multiplexer_2_out, multiplexer_3_out, multiplexer_4_out, not_1_out, not_2_out;

  Multiplexer #(.enable("false")) multiplexer_1 (.in0(IGNORE), .in1(bit1), .out(multiplexer_1_out), .sel(r_w));
  J_K_Flip_Flop j_k_ff_1 (
    .J(multiplexer_1_out), .clk(clock), .K(multiplexer_2_out), .Q(s1));  // open: Qn, preset, reset
  Multiplexer #(.enable("false")) multiplexer_2 (.in0(IGNORE), .in1(not_1_out), .out(multiplexer_2_out), .sel(r_w));
  not not_1 (not_1_out, bit1);
  Multiplexer #(.enable("false")) multiplexer_3 (.in0(IGNORE), .in1(bit0), .out(multiplexer_3_out), .sel(r_w));
  J_K_Flip_Flop j_k_ff_2 (
    .J(multiplexer_3_out), .clk(clock), .K(multiplexer_4_out), .Q(s0));  // open: Qn, preset, reset
  Multiplexer #(.enable("false")) multiplexer_4 (.in0(IGNORE), .in1(not_2_out), .out(multiplexer_4_out), .sel(r_w));
  not not_2 (not_2_out, bit0);
endmodule

module RAM_1X4 (
  input  clock,
  input  IGNORE,
  input  bit3,
  input  bit0,
  input  bit2,
  input  bit1,
  input  r_w,
  output s3,
  output s2,
  output s1,
  output s0
);

  RAM_1x2 ram_1x2_1 (.clock(clock), .IGNORE(IGNORE), .bit1(bit3), .bit0(bit2), .r_w(r_w), .s1(s3), .s0(s2));
  RAM_1x2 ram_1x2_2 (.clock(clock), .IGNORE(IGNORE), .bit1(bit1), .bit0(bit0), .r_w(r_w), .s1(s1), .s0(s0));
endmodule

module RAM_1X8 (
  input  clock,
  input  R_W,
  input  bit7,
  input  bit6,
  input  bit5,
  input  bit4,
  input  bit3,
  input  bit2,
  input  bit1,
  input  bit0,
  output s7,
  output s6,
  output s5,
  output s4,
  output s3,
  output s2,
  output s1,
  output s0
);

  RAM_1X4 ram_1x4_1 (
    .clock(clock), .IGNORE(1'b0), .bit3(bit7), .bit2(bit6), .s3(s7), .s2(s6), .s1(s5), .s0(s4), .r_w(R_W),
    .bit0(bit4), .bit1(bit5));
  RAM_1X4 ram_1x4_2 (
    .clock(clock), .IGNORE(1'b0), .bit3(bit3), .bit2(bit2), .s3(s3), .s2(s2), .s1(s1), .s0(s0), .r_w(R_W),
    .bit0(bit0), .bit1(bit1));
endmodule
