// Logisim project 1203.circ as structural Verilog: 4 circuits, main circuit main
module main (
  input  CLK,
  input  R_W,
  input  ADDRS,
  input  [7:0] \input ,
  output [7:0] \output 
);

  wire and_1_out, and_2_out, not_1_out;
  wire [7:0] demultiplexer_1_out0, demultiplexer_1_out1, ram_1x8_1_output, ram_1x8_2_output;

  RAM_1X8 ram_1x8_1 (.clock(CLK), .R_W(and_1_out), .\output (ram_1x8_1_output), .in_3(demultiplexer_1_out0));
  and and_1 (and_1_out, R_W, not_1_out);
  not not_1 (not_1_out, ADDRS);
  Demultiplexer #(.width(8), .enable("false")) demultiplexer_1 (
    .out0(demultiplexer_1_out0), .out1(demultiplexer_1_out1), .in(\input ), .sel(ADDRS));
  RAM_1X8 ram_1x8_2 (.clock(CLK), .R_W(and_2_out), .\output (ram_1x8_2_output), .in_3(demultiplexer_1_out1));
  and and_2 (and_2_out, R_W, ADDRS);
  Multiplexer #(.width(8), .enable("false")) multiplexer_1 (
    .in0(ram_1x8_1_output), .in1(ram_1x8_2_output), .out(\output ), .sel(ADDRS));
endmodule

module RAM_1X2 (
  input  clock,
  input  IGNORE,
  input  bit1,
  input  bit0,
  input  r_w,
  output s1,
  output s0
);

  wire multiplexer_1_out, multiplexer_2_out, multiplexer_3_out, multiplexer_4_out, not_1_out, not_2_out;

  Multiplexer #(.enable("false")) multiplexer_1 (.in0(IGNORE), .in1(bit1), .out(multiplexer_1_out), .sel(r_w));
  J_K_Flip_Flop j_k_ff_1 (
    .J(multiplexer_1_out), .clk(clock), .K(multiplexer_2_out), .Q(s1));  // open: Qn, preset, reset
  Multiplexer #(.enable("false")) multiplexer_2 (.in0(IGNORE), .in1(not_1_out), .out(multiplexer_2_out), .sel(r_w));
  not not_1 (not_1_out, bit1);
  Multiplexer #(.enable("false")) multiplexer_3 (.in0(IGNORE), .in1(bit0), .out(multiplexer_3_out), .sel(r_w));
  J_K_Flip_Flop j_k_ff_2 (
    .J(multiplexer_3_out), .clk(clock), .K(multiplexer_4_out), .Q(s0));  // open: Qn, preset, reset
  Multiplexer #(.enable("false")) multiplexer_4 (.in0(IGNORE), .in1(not_2_out), .out(multiplexer_4_out), .sel(r_w));
  not not_2 (not_2_out, bit0);
endmodule

module RAM_1X4 (
  input  clock,
  input  IGNORE,
  input  bit3,
  input  bit0,
  input  bit2,
  input  bit1,
  input  r_w,
  output s3,
  output s2,
  output s1,
  output s0
);

  RAM_1X2 ram_1x2_1 (.clock(clock), .IGNORE(IGNORE), .bit1(bit3), .bit0(bit2), .r_w(r_w), .s1(s3), .s0(s2));
  RAM_1X2 ram_1x2_2 (.clock(clock), .IGNORE(IGNORE), .bit1(bit1), .bit0(bit0), .r_w(r_w), .s1(s1), .s0(s0));
endmodule

module RAM_1X8 (
  input  clock,
  input  R_W,
  input  [7:0] in_3,
  output [7:0] \output 
);

  RAM_1X4 ram_1x4_1 (
    .clock(clock), .IGNORE(1'b0), .bit3(in_3[7]), .bit2(in_3[6]), .s3(\output [7]), .s2(\output [6]),
    .s1(\output [5]), .s0(\output [4]), .r_w(R_W), .bit0(in_3[4]), .bit1(in_3[5]));
  RAM_1X4 ram_1x4_2 (
    .clock(clock), .IGNORE(1'b0), .bit3(in_3[3]), .bit2(in_3[2]), .s3(\output [3]), .s2(\output [2]),
    .s1(\output [1]), .s0(\output [0]), .r_w(R_W), .bit0(in_3[0]), .bit1(in_3[1]));
endmodule
