// Logisim project 1205.circ as structural Verilog: 4 circuits, main circuit main
module main (
  input  r_w,
  input  [2:0] addrs,
  input  [7:0] in_3,
  output [7:0] out_4
);

  wire clock_1_out;
  wire [7:0] demultiplexer_1_out0, demultiplexer_1_out1, ram_4x8_1_output, ram_4x8_2_output;

  Clock clock_1 (.out(clock_1_out));
  RAM_4X8 ram_4x8_1 (
    .clock(clock_1_out), .R_W(r_w), .ADDRS(addrs[1:0]), .INPUT(demultiplexer_1_out0),
    .OUTPUT(ram_4x8_1_output));
  RAM_4X8 ram_4x8_2 (
    .clock(clock_1_out), .R_W(r_w), .ADDRS(addrs[2:1]), .INPUT(demultiplexer_1_out1),
    .OUTPUT(ram_4x8_2_output));
  Demultiplexer #(.width(8), .enable("false")) demultiplexer_1 (
    .out0(demultiplexer_1_out0), .out1(demultiplexer_1_out1), .in(in_3), .sel(addrs[2]));
  Multiplexer #(.width(8), .enable("false")) multiplexer_1 (
    .in0(ram_4x8_1_output), .in1(ram_4x8_2_output), .out(out_4), .sel(addrs[2]));
endmodule

module RAM_1X2 (
  input  clock,
  input  bit1,
  input  bit0,
  input  r_w,
  output s1,
  output s0
);

  wire multiplexer_1_out, multiplexer_2_out, multiplexer_3_out, multiplexer_4_out, not_1_out, not_2_out;

  Multiplexer #(.enable("false")) multiplexer_1 (.in0(1'b0), .in1(bit1), .out(multiplexer_1_out), .sel(r_w));
  J_K_Flip_Flop j_k_ff_1 (
    .J(multiplexer_1_out), .clk(clock), .K(multiplexer_2_out), .Q(s1));  // open: Qn, preset, reset
  Multiplexer #(.enable("false")) multiplexer_2 (.in0(1'b0), .in1(not_1_out), .out(multiplexer_2_out), .sel(r_w));
  not not_1 (not_1_out, bit1);
  Multiplexer #(.enable("false")) multiplexer_3 (.in0(1'b0), .in1(bit0), .out(multiplexer_3_out), .sel(r_w));
  J_K_Flip_Flop j_k_ff_2 (
    .J(multiplexer_3_out), .clk(clock), .K(multiplexer_4_out), .Q(s0));  // open: Qn, preset, reset
  Multiplexer #(.enable("false")) multiplexer_4 (.in0(1'b0), .in1(not_2_out), .out(multiplexer_4_out), .sel(r_w));
  not not_2 (not_2_out, bit0);
endmodule

module RAM_2X4 (
  input  CLK,
  input  R_W,
  input  [3:0] input0,
  input  [3:0] input1,
  output [3:0] output0,
  output [3:0] output1
);

  RAM_1X2 ram_1x2_1 (.clock(CLK), .bit1(input0[3]), .bit0(input0[2]), .r_w(R_W), .s1(output0[3]), .s0(output0[2]));
  RAM_1X2 ram_1x2_2 (.clock(CLK), .bit1(input0[1]), .bit0(input0[0]), .r_w(R_W), .s1(output0[1]), .s0(output0[0]));
  RAM_1X2 ram_1x2_3 (.clock(CLK), .bit1(input1[3]), .bit0(input1[2]), .r_w(R_W), .s1(output1[3]), .s0(output1[2]));
  RAM_1X2 ram_1x2_4 (.clock(CLK), .bit1(input1[1]), .bit0(input1[0]), .r_w(R_W), .s1(output1[1]), .s0(output1[0]));
endmodule

module RAM_4X8 (
  input  clock,
  input  R_W,
  input  [1:0] ADDRS,
  input  [7:0] INPUT,
  output [7:0] OUTPUT
);

  wire and_1_out, and_2_out, and_3_out, and_4_out, nor_1_out, not_1_out, not_2_out, not_3_out, not_4_out;
  wire [3:0] demultiplexer_1_out0, demultiplexer_1_out0_2, demultiplexer_1_out1, demultiplexer_1_out1_2,
       demultiplexer_1_out3, demultiplexer_1_out3_2;
  wire [7:0] demultiplexer_1_out2, multiplexer_1_out, ram_2x4_1_output0, ram_2x4_2_output0,
       ram_2x4_3_output0, ram_2x4_4_output0;

  and and_1 (and_1_out, R_W, not_1_out, not_2_out);
  not not_1 (not_1_out, ADDRS[1]);
  not not_2 (not_2_out, ADDRS[0]);
  RAM_2X4 ram_2x4_1 (
    .CLK(clock), .R_W(and_1_out), .output0(ram_2x4_1_output0[7:4]), .output1(ram_2x4_1_output0[3:0]),
    .input0(demultiplexer_1_out0_2), .input1(demultiplexer_1_out0));
  RAM_2X4 ram_2x4_2 (
    .CLK(clock), .R_W(and_2_out), .output0(ram_2x4_2_output0[7:4]), .output1(ram_2x4_2_output0[3:0]),
    .input0(demultiplexer_1_out1_2), .input1(demultiplexer_1_out1));
  and and_2 (and_2_out, R_W, not_3_out, ADDRS[0]);
  not not_3 (not_3_out, ADDRS[1]);
  Demultiplexer #(.select(2), .width(8), .enable("false")) demultiplexer_1 (
    .out0({demultiplexer_1_out0_2, demultiplexer_1_out0}),
    .out1({demultiplexer_1_out1_2, demultiplexer_1_out1}), .out2(demultiplexer_1_out2),
    .out3({demultiplexer_1_out3_2, demultiplexer_1_out3}), .in(INPUT), .sel(ADDRS));
  RAM_2X4 ram_2x4_3 (
    .CLK(clock), .R_W(and_3_out), .output0(ram_2x4_3_output0[7:4]), .output1(ram_2x4_3_output0[3:0]),
    .input0(demultiplexer_1_out2[7:4]), .input1(demultiplexer_1_out2[3:0]));
  and and_3 (and_3_out, R_W, ADDRS[1], not_4_out);
  not not_4 (not_4_out, ADDRS[0]);
  RAM_2X4 ram_2x4_4 (
    .CLK(clock), .R_W(and_4_out), .output0(ram_2x4_4_output0[7:4]), .output1(ram_2x4_4_output0[3:0]),
    .input0(demultiplexer_1_out3_2), .input1(demultiplexer_1_out3));
  and and_4 (and_4_out, R_W, ADDRS[1], ADDRS[0]);
  Multiplexer #(.select(2), .width(8), .enable("false")) multiplexer_1 (
    .in0(ram_2x4_1_output0), .in1(ram_2x4_2_output0), .in2(ram_2x4_3_output0), .in3(ram_2x4_4_output0),
    .out(multiplexer_1_out), .sel(ADDRS));
  nor nor_1 (nor_1_out, clock, R_W);
  Multiplexer #(.width(8), .enable("false")) multiplexer_2 (
    .in0({8{1'b0}}), .in1(multiplexer_1_out), .out(OUTPUT), .sel(nor_1_out));
endmodule
