// Logisim project Guia_1301.circ as structural Verilog: 1 circuit, main circuit main
module main (
  input  SET,
  input  clr
);

  wire clock_1_out, j_k_ff_2_q, j_k_ff_3_q, j_k_ff_4_q, j_k_ff_5_q;

  J_K_Flip_Flop j_k_ff_1 (.J(1'b1), .clk(j_k_ff_2_q), .K(1'b1), .preset(SET), .reset(clr));  // open: Q, Qn
  J_K_Flip_Flop j_k_ff_2 (.J(1'b1), .clk(j_k_ff_3_q), .K(1'b1), .Q(j_k_ff_2_q), .preset(SET), .reset(clr));  // open: Qn
  J_K_Flip_Flop j_k_ff_3 (.J(1'b1), .clk(j_k_ff_4_q), .K(1'b1), .Q(j_k_ff_3_q), .preset(SET), .reset(clr));  // open: Qn
  J_K_Flip_Flop j_k_ff_4 (.J(1'b1), .clk(j_k_ff_5_q), .K(1'b1), .Q(j_k_ff_4_q), .preset(SET), .reset(clr));  // open: Qn
  Clock clock_1 (.out(clock_1_out));
  J_K_Flip_Flop j_k_ff_5 (
    .J(1'b1), .clk(clock_1_out), .K(1'b1), .Q(j_k_ff_5_q), .preset(SET), .reset(clr));  // open: Qn
endmodule
