// Logisim project Guia_1302.circ as structural Verilog: 1 circuit, main circuit main
module main (
);

  wire clock_1_out, j_k_ff_2_qn, j_k_ff_3_qn, j_k_ff_4_qn, j_k_ff_5_qn;

  J_K_Flip_Flop j_k_ff_1 (.J(1'b1), .clk(j_k_ff_2_qn), .K(1'b1));  // open: Q, Qn, preset, reset
  J_K_Flip_Flop j_k_ff_2 (.J(1'b1), .clk(j_k_ff_3_qn), .K(1'b1), .Qn(j_k_ff_2_qn));  // open: Q, preset, reset
  J_K_Flip_Flop j_k_ff_3 (.J(1'b1), .clk(j_k_ff_4_qn), .K(1'b1), .Qn(j_k_ff_3_qn));  // open: Q, preset, reset
  J_K_Flip_Flop j_k_ff_4 (.J(1'b1), .clk(j_k_ff_5_qn), .K(1'b1), .Qn(j_k_ff_4_qn));  // open: Q, preset, reset
  Clock clock_1 (.out(clock_1_out));
  J_K_Flip_Flop j_k_ff_5 (.J(1'b1), .clk(clock_1_out), .K(1'b1), .Qn(j_k_ff_5_qn));  // open: Q, preset, reset
endmodule
