// Logisim project Guia_1303.circ as structural Verilog: 1 circuit, main circuit main
module main (
  input  SET
);

  wire and_1_out, clock_1_out, displaydecoder_1_p1, displaydecoder_1_p2, displaydecoder_1_p3,
       displaydecoder_1_p4, displaydecoder_1_p5, displaydecoder_1_p6, displaydecoder_1_p7, j_k_ff_2_qn,
       j_k_ff_3_qn, j_k_ff_4_qn, not_1_out, not_2_out;
  wire [3:0] j_k_ff_4_q;

  J_K_Flip_Flop j_k_ff_1 (
    .J(1'b1), .clk(j_k_ff_2_qn), .K(1'b1), .Q(j_k_ff_4_q[3]), .preset(SET), .reset(and_1_out));  // open: Qn
  J_K_Flip_Flop j_k_ff_2 (
    .J(1'b1), .clk(j_k_ff_3_qn), .K(1'b1), .Q(j_k_ff_4_q[2]), .Qn(j_k_ff_2_qn), .preset(SET),
    .reset(and_1_out));
  J_K_Flip_Flop j_k_ff_3 (
    .J(1'b1), .clk(j_k_ff_4_qn), .K(1'b1), .Q(j_k_ff_4_q[1]), .Qn(j_k_ff_3_qn), .preset(SET),
    .reset(and_1_out));
  Clock clock_1 (.out(clock_1_out));
  J_K_Flip_Flop j_k_ff_4 (
    .J(1'b1), .clk(clock_1_out), .K(1'b1), .Q(j_k_ff_4_q[0]), .Qn(j_k_ff_4_qn), .preset(SET),
    .reset(and_1_out));
  not not_1 (not_1_out, j_k_ff_4_q[2]);
  not not_2 (not_2_out, j_k_ff_4_q[0]);
  and and_1 (and_1_out, j_k_ff_4_q[3], not_1_out, j_k_ff_4_q[1], not_2_out);
  // DisplayDecoder displaydecoder_1: pin names not known; wires that end beside it: displaydecoder_1_p1, displaydecoder_1_p2, displaydecoder_1_p3, displaydecoder_1_p4, displaydecoder_1_p5, displaydecoder_1_p6, displaydecoder_1_p7
  _7_Segment_Display u_7_segment_display_1 (
    .g(displaydecoder_1_p7), .f(displaydecoder_1_p6), .a(displaydecoder_1_p1), .b(displaydecoder_1_p2),
    .e(displaydecoder_1_p5), .d(displaydecoder_1_p4), .c(displaydecoder_1_p3));  // open: dp
endmodule
