// Logisim project Guia_1304.circ as structural Verilog: 1 circuit, main circuit main
module main (
  input  CLEAR
);

  wire and_1_out, clock_1_out, displaydecoder_1_p1, displaydecoder_1_p2, displaydecoder_1_p3,
       displaydecoder_1_p4, displaydecoder_1_p6, displaydecoder_1_p7, displaydecoder_1_p8, j_k_ff_1_qn,
       j_k_ff_2_qn, j_k_ff_3_qn, j_k_ff_4_qn, not_1_out, not_2_out;
  wire [3:0] displaydecoder_1_p5;

  not not_1 (not_1_out, j_k_ff_4_qn);
  and and_1 (and_1_out, not_1_out, j_k_ff_3_qn, not_2_out, j_k_ff_1_qn);
  not not_2 (not_2_out, j_k_ff_2_qn);
  J_K_Flip_Flop j_k_ff_1 (
    .J(1'b1), .clk(displaydecoder_1_p5[2]), .K(1'b1), .Q(displaydecoder_1_p5[3]), .Qn(j_k_ff_1_qn),
    .preset(and_1_out), .reset(CLEAR));
  J_K_Flip_Flop j_k_ff_2 (
    .J(1'b1), .clk(displaydecoder_1_p5[1]), .K(1'b1), .Q(displaydecoder_1_p5[2]), .Qn(j_k_ff_2_qn),
    .preset(and_1_out), .reset(CLEAR));
  // DisplayDecoder displaydecoder_1: pin names not known; wires that end beside it: displaydecoder_1_p1, displaydecoder_1_p2, displaydecoder_1_p3, displaydecoder_1_p4, displaydecoder_1_p5, displaydecoder_1_p6, displaydecoder_1_p7, displaydecoder_1_p8
  J_K_Flip_Flop j_k_ff_3 (
    .J(1'b1), .clk(displaydecoder_1_p5[0]), .K(1'b1), .Q(displaydecoder_1_p5[1]), .Qn(j_k_ff_3_qn),
    .preset(and_1_out), .reset(CLEAR));
  J_K_Flip_Flop j_k_ff_4 (
    .J(1'b1), .clk(clock_1_out), .K(1'b1), .Q(displaydecoder_1_p5[0]), .Qn(j_k_ff_4_qn), .preset(and_1_out),
    .reset(CLEAR));
  _7_Segment_Display u_7_segment_display_1 (
    .g(displaydecoder_1_p8), .f(displaydecoder_1_p7), .a(displaydecoder_1_p1), .b(displaydecoder_1_p2),
    .e(displaydecoder_1_p6), .d(displaydecoder_1_p4), .c(displaydecoder_1_p3));  // open: dp
  Clock clock_1 (.out(clock_1_out));
endmodule
