// Logisim project Guia_1305.circ as structural Verilog: 1 circuit, main circuit main
module main (
);

  wire and_1_out, and_2_out, and_3_out, clock_1_out, not_1_out, not_2_out, t_ff_1_q, t_ff_2_q, t_ff_3_q,
       t_ff_4_q;

  Clock clock_1 (.out(clock_1_out));
  T_Flip_Flop t_ff_1 (.clk(clock_1_out), .T(and_1_out), .Q(t_ff_1_q), .reset(and_3_out));  // open: Qn, preset
  and and_1 (and_1_out, t_ff_2_q, and_2_out);
  T_Flip_Flop t_ff_2 (.clk(clock_1_out), .T(and_2_out), .Q(t_ff_2_q), .reset(and_3_out));  // open: Qn, preset
  and and_2 (and_2_out, t_ff_3_q, t_ff_4_q);
  T_Flip_Flop t_ff_3 (.clk(clock_1_out), .T(t_ff_4_q), .Q(t_ff_3_q), .reset(and_3_out));  // open: Qn, preset
  T_Flip_Flop t_ff_4 (.clk(clock_1_out), .T(1'b1), .Q(t_ff_4_q), .reset(and_3_out));  // open: Qn, preset
  and and_3 (and_3_out, t_ff_4_q, not_1_out, not_2_out, t_ff_1_q);
  not not_1 (not_1_out, t_ff_3_q);
  not not_2 (not_2_out, t_ff_2_q);
endmodule
