// Logisim project Q01.circ as structural Verilog: 1 circuit, main circuit main
module main (
  input  a,
  input  b,
  input  c,
  input  d,
  input  a_2,
  input  b_2,
  input  c_2,
  input  d_2,
  input  A_3,
  input  B_3,
  input  C_3,
  input  D_3,
  input  A_4,
  input  B_4,
  input  C_4,
  input  D_4,
  output out_17,
  output out_18,
  output out_19,
  output out_20
);

  wire and_1_out, and_2_out, and_3_out, nand_1_out, nand_2_out, nand_3_out, nand_4_out, nand_5_out,
       nand_6_out, nand_7_out, nand_8_out, nand_9_out, nand_10_out, nand_11_out, nand_12_out, nand_13_out,
       nand_14_out, nand_15_out, nor_1_out, nor_2_out, nor_3_out, nor_4_out, nor_5_out, nor_6_out, nor_7_out,
       nor_8_out, nor_9_out, nor_10_out, nor_11_out, nor_12_out, nor_13_out, nor_14_out, nor_15_out,
       not_1_out, not_2_out, not_3_out, not_4_out, not_5_out, not_6_out, not_7_out, not_8_out, or_1_out,
       or_2_out, or_3_out;

  not not_1 (not_1_out, a_2);
  not not_2 (not_2_out, A_4);
  not not_3 (not_3_out, c_2);
  not not_4 (not_4_out, b_2);
  not not_5 (not_5_out, B_4);
  not not_6 (not_6_out, d_2);
  not not_7 (not_7_out, C_4);
  not not_8 (not_8_out, D_4);
  and and_1 (and_1_out, not_4_out, c_2);
  and and_2 (and_2_out, not_1_out, b_2, not_3_out);
  and and_3 (and_3_out, a_2, b_2, d_2);
  or or_1 (or_1_out, B_4, C_4);
  or or_2 (or_2_out, A_4, not_5_out, not_7_out);
  or or_3 (or_3_out, not_2_out, not_5_out, D_4);
  or or_4 (out_17, and_1_out, and_2_out, and_3_out);
  and and_4 (out_19, or_1_out, or_2_out, or_3_out);
  nand nand_1 (nand_1_out, a, a);
  nor nor_1 (nor_1_out, A_3, A_3);
  nand nand_2 (nand_2_out, b, b, b);
  nor nor_2 (nor_2_out, B_3, B_3);
  nand nand_3 (nand_3_out, c, c);
  nor nor_3 (nor_3_out, C_3, C_3);
  nand nand_4 (nand_4_out, d, d, d);
  nor nor_4 (nor_4_out, D_3, D_3);
  nand nand_5 (nand_5_out, nand_2_out, c);
  nand nand_6 (nand_6_out, nand_1_out, b, nand_3_out);
  nand nand_7 (nand_7_out, a, b, c);
  nor nor_5 (nor_5_out, B_3, C_3);
  nor nor_6 (nor_6_out, A_3, nor_2_out, nor_3_out);
  nor nor_7 (nor_7_out, nor_1_out, nor_2_out, D_3);
  nand nand_8 (nand_8_out, nand_5_out, nand_5_out);
  nand nand_9 (nand_9_out, nand_6_out, nand_6_out);
  nand nand_10 (nand_10_out, nand_7_out, nand_7_out);
  nor nor_8 (nor_8_out, nor_5_out, nor_5_out);
  nor nor_9 (nor_9_out, nor_6_out, nor_6_out);
  nor nor_10 (nor_10_out, nor_7_out, nor_7_out);
  nand nand_11 (nand_11_out, nand_8_out, nand_8_out);
  nand nand_12 (nand_12_out, nand_11_out, nand_13_out);
  nand nand_13 (nand_13_out, nand_9_out, nand_9_out);
  nand nand_14 (nand_14_out, nand_10_out, nand_10_out);
  nor nor_11 (nor_11_out, nor_8_out, nor_8_out);
  nor nor_12 (nor_12_out, nor_11_out, nor_13_out);
  nor nor_13 (nor_13_out, nor_9_out, nor_9_out);
  nor nor_14 (nor_14_out, nor_10_out, nor_10_out);
  nand nand_15 (nand_15_out, nand_12_out, nand_12_out);
  nand nand_16 (out_18, nand_15_out, nand_14_out);
  nor nor_15 (nor_15_out, nor_12_out, nor_12_out);
  nor nor_16 (out_20, nor_15_out, nor_14_out);

  // Notes on the sheet:
  //   a/c)
  //   b/d)
  //   f)
  //   e)
  //   AND
  //   AND
  //   AND
  //   OR
  //   OR
  //   OR
  //   OR
  //   OR
  //   OR
  //   OR
endmodule
