// Logisim project Q03b.circ as structural Verilog: 1 circuit, main circuit main
module main (
  input  b,
  input  a,
  input  c,
  output out_4
);

  wire multiplexer_1_out, multiplexer_2_out, not_1_out, not_2_out, not_3_out;

  not not_1 (not_1_out, b);
  not not_2 (not_2_out, b);
  Multiplexer #(.enable("false")) multiplexer_1 (.in0(b), .in1(not_1_out), .out(multiplexer_1_out), .sel(c));
  Multiplexer #(.enable("false")) multiplexer_2 (.in0(not_2_out), .in1(b), .out(multiplexer_2_out), .sel(not_3_out));
  not not_3 (not_3_out, c);
  Multiplexer #(.enable("false")) multiplexer_3 (
    .in0(multiplexer_1_out), .in1(multiplexer_2_out), .out(out_4), .sel(a));
endmodule
