// Logisim project ffTa.circ as structural Verilog: 1 circuit, main circuit main
module main (
  input  in_1,
  input  in_2,
  input  in_3,
  input  in_4,
  input  in_5,
  output out_6,
  output out_7,
  output out_8,
  output out_9,
  output out_10,
  output out_11
);

  wire and_1_out, and_2_out, clock_1_out, not_1_out;

  Clock clock_1 (.out(clock_1_out));
  not not_1 (not_1_out, in_2);
  and and_1 (and_1_out, out_7, in_1, clock_1_out);
  and and_2 (and_2_out, clock_1_out, in_1, out_6);
  T_Flip_Flop t_ff_1 (.clk(not_1_out), .T(in_3), .Q(out_8), .Qn(out_9));  // open: preset, reset, en
  T_Flip_Flop t_ff_2 (.clk(in_4), .T(in_5), .Q(out_10), .Qn(out_11));  // open: preset, reset, en
  nor nor_1 (out_6, and_1_out, out_7);
  nor nor_2 (out_7, out_6, and_2_out);
endmodule
