// Logisim project ALU4BITS.circ as structural Verilog
module SomadorCompleto (
  input  cIn,
  input  a,
  input  b,
  output s,
  output cout
);

  wire and_1_out, and_2_out, xor_1_out;

  and and_1 (and_1_out, a, b);
  xor xor_1 (xor_1_out, a, b);
  and and_2 (and_2_out, cIn, xor_1_out);
  or or_1 (cout, and_1_out, and_2_out);
  xor xor_2 (s, cIn, xor_1_out);
endmodule

module ALU1BIT (
  input  Binvert,
  input  cin,
  input  a,
  input  b,
  input  op0,
  input  op1,
  output s,
  output cout
);

  wire and_1_out, mux2_1_out_4, not_1_out, not_2_out, or_1_out, somadorcompleto_1_s;

  not not_1 (not_1_out, b);
  mux2 mux2_1 (.in_1(b), .in_2(not_1_out), .in_3(Binvert), .out_4(mux2_1_out_4));
  and and_1 (and_1_out, a, mux2_1_out_4);
  or or_1 (or_1_out, a, mux2_1_out_4);
  not not_2 (not_2_out, a);
  SomadorCompleto somadorcompleto_1 (.a(a), .b(mux2_1_out_4), .cIn(cin), .cout(cout), .s(somadorcompleto_1_s));
  mux4 mux4_1 (.m(and_1_out), .n(or_1_out), .o(not_2_out), .p(somadorcompleto_1_s), .op1(op0), .op0(op1), .s(s));
endmodule

module mux4 (
  input  m,
  input  n,
  input  o,
  input  p,
  input  op1,
  input  op0,
  output s
);

  wire and_1_out, and_2_out, and_3_out, and_4_out, not_1_out, not_2_out, not_3_out, not_4_out;

  not not_1 (not_1_out, op1);
  not not_2 (not_2_out, op0);
  not not_3 (not_3_out, op1);
  not not_4 (not_4_out, op0);
  and and_1 (and_1_out, m, not_1_out, not_2_out);
  and and_2 (and_2_out, n, not_3_out, op0);
  and and_3 (and_3_out, o, op1, not_4_out);
  and and_4 (and_4_out, p, op1, op0);
  or or_1 (s, and_1_out, and_2_out, and_3_out, and_4_out);
endmodule

module mux2 (
  input  in_1,
  input  in_2,
  input  in_3,
  output out_4
);

  wire and_1_out, and_2_out, not_1_out;

  not not_1 (not_1_out, in_3);
  and and_1 (and_1_out, in_1, not_1_out);
  and and_2 (and_2_out, in_2, in_3);
  or or_1 (out_4, and_1_out, and_2_out);
endmodule

module ALU4BITS (
  input  B3,
  input  B2,
  input  B1,
  input  B0,
  input  A3,
  input  A2,
  input  A1,
  input  A0,
  input  BINVERT,
  input  OP0,
  input  OP1,
  output S3,
  output S2,
  output S1,
  output S0,
  output COUT
);

  wire alu1bit_1_cout, alu1bit_2_cout, alu1bit_3_cout;

  ALU1BIT alu1bit_1 (
    .a(A0), .b(B0), .Binvert(BINVERT), .cin(BINVERT), .cout(alu1bit_1_cout), .op0(OP0), .op1(OP1), .s(S3));
  ALU1BIT alu1bit_2 (
    .a(A1), .b(B1), .Binvert(BINVERT), .cin(alu1bit_1_cout), .cout(alu1bit_2_cout), .op0(OP0), .op1(OP1),
    .s(S2));
  ALU1BIT alu1bit_3 (
    .a(A2), .b(B2), .Binvert(BINVERT), .cin(alu1bit_2_cout), .cout(alu1bit_3_cout), .op0(OP0), .op1(OP1),
    .s(S1));
  ALU1BIT alu1bit_4 (
    .a(A3), .b(B3), .Binvert(BINVERT), .cin(alu1bit_3_cout), .cout(COUT), .op0(OP0), .op1(OP1), .s(S0));
endmodule
