// Logisim project Somador 4 bits.circ as structural Verilog
module MeioSomador (
  input  x0,
  input  y0,
  output saida,
  output carryout
);

  xor xor_1 (saida, x0, y0);
  and and_1 (carryout, x0, y0);
endmodule

module somadorCompleto (
  input  carryIn,
  input  x1,
  input  y1,
  output saida,
  output carryout
);

  wire meiosomador_1_carryout, meiosomador_1_saida, meiosomador_2_carryout;

  MeioSomador meiosomador_1 (.x0(x1), .y0(y1), .carryout(meiosomador_1_carryout), .saida(meiosomador_1_saida));
  or or_1 (carryout, meiosomador_1_carryout, meiosomador_2_carryout);
  MeioSomador meiosomador_2 (.x0(carryIn), .y0(meiosomador_1_saida), .carryout(meiosomador_2_carryout), .saida(saida));
endmodule

module Somador4bits (
  input  carryin,
  input  x0,
  input  y0,
  input  x1,
  input  y1,
  input  x2,
  input  y2,
  input  x3,
  input  y3,
  output s0,
  output s1,
  output s2,
  output s3,
  output carryout
);

  wire somadorcompleto_1_carryout, somadorcompleto_2_carryout, somadorcompleto_3_carryout;

  somadorCompleto somadorcompleto_1 (
    .x1(x0), .y1(y0), .carryIn(carryin), .carryout(somadorcompleto_1_carryout), .saida(s0));
  somadorCompleto somadorcompleto_2 (
    .x1(x1), .y1(y1), .carryIn(somadorcompleto_1_carryout), .carryout(somadorcompleto_2_carryout), .saida(s1));
  somadorCompleto somadorcompleto_3 (
    .x1(x2), .y1(y2), .carryIn(somadorcompleto_2_carryout), .carryout(somadorcompleto_3_carryout), .saida(s2));
  somadorCompleto somadorcompleto_4 (
    .x1(x3), .y1(y3), .carryIn(somadorcompleto_3_carryout), .carryout(carryout), .saida(s3));
endmodule

module DecodificadorHEXA (
  input  A0,
  input  A1,
  input  A2,
  input  A3,
  output A,
  output B,
  output C,
  output D,
  output E,
  output F,
  output G
);

  wire and_1_out, and_2_out, and_3_out, and_4_out, and_5_out, and_6_out, and_7_out, and_8_out, and_9_out,
       and_10_out, and_11_out, and_12_out, and_13_out, and_14_out, and_15_out, and_16_out, and_17_out,
       and_18_out, and_19_out, and_20_out, and_21_out, and_22_out, and_23_out, and_24_out, and_25_out,
       and_26_out, and_27_out, and_28_out, and_29_out, and_30_out, and_31_out, and_32_out, and_33_out,
       and_34_out, and_35_out, and_36_out, not_1_out, not_2_out, not_3_out, not_4_out, not_5_out, not_6_out,
       not_7_out, not_8_out, not_9_out, not_10_out, not_11_out, not_12_out, not_13_out, not_14_out,
       not_15_out, not_16_out, not_17_out, not_18_out, not_19_out, not_20_out, not_21_out, not_22_out,
       not_23_out, not_24_out, not_25_out, not_26_out, not_27_out, not_28_out, not_29_out, not_30_out,
       not_31_out, not_32_out, not_33_out, not_34_out, not_35_out, not_36_out, not_37_out, not_38_out,
       not_39_out, not_40_out, not_41_out, not_42_out, not_43_out, not_44_out, not_45_out, not_46_out;

  not not_1 (not_1_out, A1);
  and and_1 (and_1_out, not_1_out, not_2_out);
  not not_2 (not_2_out, A3);
  not not_3 (not_3_out, A0);
  and and_2 (and_2_out, not_3_out, A2);
  not not_4 (not_4_out, A0);
  and and_3 (and_3_out, not_4_out, A1, A3);
  and and_4 (and_4_out, A1, A2);
  and and_5 (and_5_out, A0, not_5_out, not_6_out);
  not not_5 (not_5_out, A1);
  not not_6 (not_6_out, A2);
  and and_6 (and_6_out, A0, not_7_out);
  not not_7 (not_7_out, A3);
  not not_8 (not_8_out, A0);
  and and_7 (and_7_out, not_8_out, not_9_out);
  not not_9 (not_9_out, A1);
  not not_10 (not_10_out, A0);
  not not_11 (not_11_out, A2);
  and and_8 (and_8_out, not_10_out, not_11_out, not_12_out);
  not not_12 (not_12_out, A3);
  not not_13 (not_13_out, A1);
  and and_9 (and_9_out, not_13_out, not_14_out);
  not not_14 (not_14_out, A2);
  not not_15 (not_15_out, A1);
  and and_10 (and_10_out, not_15_out, not_16_out);
  not not_16 (not_16_out, A3);
  not not_17 (not_17_out, A0);
  and and_11 (and_11_out, not_17_out, A2, A3);
  and and_12 (and_12_out, A0, not_18_out, A3);
  not not_18 (not_18_out, A2);
  not not_19 (not_19_out, A0);
  and and_13 (and_13_out, not_19_out, not_20_out);
  not not_20 (not_20_out, A2);
  not not_21 (not_21_out, A0);
  and and_14 (and_14_out, not_21_out, A3);
  not not_22 (not_22_out, A2);
  and and_15 (and_15_out, not_22_out, A3);
  not not_23 (not_23_out, A0);
  and and_16 (and_16_out, not_23_out, A1);
  and and_17 (and_17_out, A0, not_24_out);
  not not_24 (not_24_out, A1);
  not not_25 (not_25_out, A0);
  not not_26 (not_26_out, A1);
  and and_18 (and_18_out, not_25_out, not_26_out, not_27_out);
  not not_27 (not_27_out, A3);
  not not_28 (not_28_out, A1);
  and and_19 (and_19_out, not_28_out, A2, A3);
  not not_29 (not_29_out, A2);
  and and_20 (and_20_out, A1, not_29_out, A3);
  and and_21 (and_21_out, A1, A2, not_30_out);
  not not_30 (not_30_out, A3);
  and and_22 (and_22_out, A0, not_31_out, not_32_out);
  not not_31 (not_31_out, A2);
  not not_32 (not_32_out, A3);
  not not_33 (not_33_out, A1);
  and and_23 (and_23_out, not_33_out, not_34_out);
  not not_34 (not_34_out, A3);
  and and_24 (and_24_out, A2, not_35_out);
  not not_35 (not_35_out, A3);
  and and_25 (and_25_out, A0, A2);
  and and_26 (and_26_out, A0, A1);
  not not_36 (not_36_out, A2);
  and and_27 (and_27_out, not_36_out, not_37_out);
  not not_37 (not_37_out, A3);
  not not_38 (not_38_out, A0);
  and and_28 (and_28_out, not_38_out, A1, not_39_out);
  not not_39 (not_39_out, A2);
  and and_29 (and_29_out, A1, not_40_out);
  not not_40 (not_40_out, A3);
  and and_30 (and_30_out, A0, not_41_out);
  not not_41 (not_41_out, A1);
  and and_31 (and_31_out, A0, A2);
  not not_42 (not_42_out, A1);
  and and_32 (and_32_out, not_42_out, A2);
  and and_33 (and_33_out, A2, not_43_out);
  not not_43 (not_43_out, A3);
  not not_44 (not_44_out, A0);
  and and_34 (and_34_out, not_44_out, A1, not_45_out);
  not not_45 (not_45_out, A2);
  and and_35 (and_35_out, A0, not_46_out);
  not not_46 (not_46_out, A1);
  and and_36 (and_36_out, A0, A3);
  or or_1 (C, and_13_out, and_14_out, and_15_out, and_16_out, and_17_out);
  or or_2 (D, and_18_out, and_19_out, and_20_out, and_21_out, and_22_out);
  or or_3 (E, and_23_out, and_24_out, and_25_out, and_26_out);
  or or_4 (F, and_27_out, and_28_out, and_29_out, and_30_out, and_31_out);
  or or_5 (G, and_32_out, and_33_out, and_34_out, and_35_out, and_36_out);
  or or_6 (A, and_1_out, and_2_out, and_3_out, and_4_out, and_5_out, and_6_out);
  or or_7 (B, and_7_out, and_8_out, and_9_out, and_10_out, and_11_out, and_12_out);
endmodule

module Calculadora4bits (
  input  a0,
  input  a1,
  input  cin,
  input  a2,
  input  a3,
  input  b0,
  input  b1,
  input  b2,
  input  b3,
  output s0,
  output s1,
  output s2,
  output s3,
  output cout
);

  wire decodificadorhexa_1_a, decodificadorhexa_1_b, decodificadorhexa_1_c, decodificadorhexa_1_d,
       decodificadorhexa_1_e, decodificadorhexa_1_f, decodificadorhexa_1_g, decodificadorhexa_2_a,
       decodificadorhexa_2_b, decodificadorhexa_2_c, decodificadorhexa_2_d, decodificadorhexa_2_e,
       decodificadorhexa_2_f, decodificadorhexa_2_g, decodificadorhexa_3_a, decodificadorhexa_3_b,
       decodificadorhexa_3_c, decodificadorhexa_3_d, decodificadorhexa_3_e, decodificadorhexa_3_f,
       decodificadorhexa_3_g;

  Somador4bits somador4bits_1 (
    .x0(a0), .y0(b0), .x1(a1), .y1(b1), .x2(a2), .y2(b2), .x3(a3), .y3(b3), .carryin(cin), .carryout(cout),
    .s0(s0), .s1(s1), .s2(s2), .s3(s3));
  DecodificadorHEXA decodificadorhexa_1 (
    .A0(b3), .A1(b2), .A2(b1), .A3(b0), .A(decodificadorhexa_1_a), .B(decodificadorhexa_1_b),
    .C(decodificadorhexa_1_c), .D(decodificadorhexa_1_d), .E(decodificadorhexa_1_e),
    .F(decodificadorhexa_1_f), .G(decodificadorhexa_1_g));
  DecodificadorHEXA decodificadorhexa_2 (
    .A0(a3), .A1(a2), .A2(a1), .A3(a0), .A(decodificadorhexa_2_a), .B(decodificadorhexa_2_b),
    .C(decodificadorhexa_2_c), .D(decodificadorhexa_2_d), .E(decodificadorhexa_2_e),
    .F(decodificadorhexa_2_f), .G(decodificadorhexa_2_g));
  _7_Segment_Display u_7_segment_display_1 (
    .g(decodificadorhexa_1_g), .f(decodificadorhexa_1_f), .a(decodificadorhexa_1_a),
    .b(decodificadorhexa_1_b), .e(decodificadorhexa_1_e), .d(decodificadorhexa_1_d), .c(decodificadorhexa_1_c));  // open: dp
  _7_Segment_Display u_7_segment_display_2 (
    .g(decodificadorhexa_2_g), .f(decodificadorhexa_2_f), .a(decodificadorhexa_2_a),
    .b(decodificadorhexa_2_b), .e(decodificadorhexa_2_e), .d(decodificadorhexa_2_d), .c(decodificadorhexa_2_c));  // open: dp
  DecodificadorHEXA decodificadorhexa_3 (
    .A0(s3), .A1(s2), .A2(s1), .A3(s0), .A(decodificadorhexa_3_a), .B(decodificadorhexa_3_b),
    .C(decodificadorhexa_3_c), .D(decodificadorhexa_3_d), .E(decodificadorhexa_3_e),
    .F(decodificadorhexa_3_f), .G(decodificadorhexa_3_g));
  _7_Segment_Display u_7_segment_display_3 (
    .g(decodificadorhexa_3_g), .f(decodificadorhexa_3_f), .a(decodificadorhexa_3_a),
    .b(decodificadorhexa_3_b), .e(decodificadorhexa_3_e), .d(decodificadorhexa_3_d), .c(decodificadorhexa_3_c));  // open: dp
endmodule
